# Fritzing sketch tala (saved by Fritzing 0.9.3b)

parts:
  Raspberry_Pi_Zero1 = Raspberry Pi Zero
  Squix1 = OLED 0.96" 128x64 I2C SSD1306
  kEYPAD_MATRICIAL_1 = KEYPAD 4x3
  HC-1 = HC-12 Module
  Antenna1 = HC-12 Antenna

nets:
  3V3: Raspberry_Pi_Zero1.3v3, Raspberry_Pi_Zero1.3V3, Squix1.VCC, HC-1.VCC
  N1: Raspberry_Pi_Zero1.GPIO2, Squix1.SCA
  N2: Raspberry_Pi_Zero1.GPIO3, Squix1.SCL
  GND: Raspberry_Pi_Zero1.GND, Squix1.GND, HC-1.GND
  N3: Raspberry_Pi_Zero1.GPIO17, kEYPAD_MATRICIAL_1.Col_1
  N4: Raspberry_Pi_Zero1.GPIO27, kEYPAD_MATRICIAL_1.Col_2
  N5: Raspberry_Pi_Zero1.GPIO22, kEYPAD_MATRICIAL_1.Col_3
  N6: Raspberry_Pi_Zero1.GPIO6, kEYPAD_MATRICIAL_1.Row_4
  N7: Raspberry_Pi_Zero1.GPIO13, kEYPAD_MATRICIAL_1.Row_3
  N8: Raspberry_Pi_Zero1.GPIO19, kEYPAD_MATRICIAL_1.Row_2
  N9: Raspberry_Pi_Zero1.GPIO26, kEYPAD_MATRICIAL_1.Row_1
  N10: Raspberry_Pi_Zero1.GPIO15, HC-1.TXD
  N11: Raspberry_Pi_Zero1.GPIO14, HC-1.RXD
  N12: HC-1.ANT, Antenna1.ANT

custom parts:
  KEYPAD 4x3: KEYPAD matricial de 12 botones, 4 filas x 3 columnas
  HC-12 Module: HC-12 433Mhz Module
  HC-12 Antenna: Antenna for HC-12 433Mhz Module
